// Logisim project Somadores.circ as structural Verilog: 7 circuits, main circuit main
module main (
  input  [1:0] XY,
  input  [3:0] A,
  input  [3:0] B,
  output OverFlow,
  output [3:0] S,
  output OverFlow_2,
  output [3:0] S_2,
  output [3:0] S_3,
  output [3:0] S_4
);

  Somador_4Bits somador_4bits_1 (.Overflow(OverFlow), .B(B), .A(A), .Saida(S_3));
  Subtrator_4Bit subtrator_4bit_1 (.B(B), .Overflow(OverFlow_2), .A(A), .Saida(S_4));
  \Rotação_Esq  \rotação_esq_1  (.ABCD(A), .XY(XY), .ABCD_2(S));
  \Rotação_Dir  \rotação_dir_1  (.ABCD(A), .XY(XY), .ABCD_2(S_2));
endmodule

module Somador_1Bit (
  input  A,
  input  B,
  input  C,
  output S,
  output Vai_1
);

  wire and_1_out, and_2_out, or_1_out, xor_1_out;

  xor xor_1 (xor_1_out, C, B);
  and and_1 (and_1_out, C, B);
  or or_1 (or_1_out, C, B);
  and and_2 (and_2_out, or_1_out, A);
  xor xor_2 (S, xor_1_out, A);
  or or_2 (Vai_1, and_1_out, and_2_out);
endmodule

module Somador_4Bits (
  input  [3:0] A,
  input  [3:0] B,
  output Overflow,
  output [3:0] Saida
);

  wire somador_1bit_2_vai_1, somador_1bit_3_vai_1, somador_1bit_4_vai_1;

  // Probe on B
  Somador_1Bit somador_1bit_1 (.S(Saida[3]), .Vai_1(Overflow), .A(A[3]), .B(B[3]), .C(somador_1bit_2_vai_1));
  Somador_1Bit somador_1bit_2 (
    .S(Saida[2]), .Vai_1(somador_1bit_2_vai_1), .A(A[2]), .B(B[2]), .C(somador_1bit_3_vai_1));
  // Probe on Saida
  Somador_1Bit somador_1bit_3 (
    .S(Saida[1]), .Vai_1(somador_1bit_3_vai_1), .A(A[1]), .B(B[1]), .C(somador_1bit_4_vai_1));
  Somador_1Bit somador_1bit_4 (.S(Saida[0]), .Vai_1(somador_1bit_4_vai_1), .A(A[0]), .B(B[0]), .C(1'b0));
  // Probe on A
endmodule

module Subtrator_1Bit (
  input  A,
  input  B,
  input  C,
  output S,
  output Vai_1
);

  wire and_1_out, and_2_out, or_1_out, xor_1_out;

  xor xor_1 (xor_1_out, C, B);
  and and_1 (and_1_out, C, B);
  or or_1 (or_1_out, C, B);
  and and_2 (and_2_out, or_1_out, ~A);  // AND_Gate
  xor xor_2 (S, xor_1_out, A);
  or or_2 (Vai_1, and_1_out, and_2_out);
endmodule

module Subtrator_4Bit (
  input  [3:0] A,
  input  [3:0] B,
  output Overflow,
  output [3:0] Saida
);

  wire subtrator_1bit_2_vai_1, subtrator_1bit_3_vai_1, subtrator_1bit_4_vai_1;

  // Probe on B
  Subtrator_1Bit subtrator_1bit_1 (.S(Saida[3]), .Vai_1(Overflow), .A(A[3]), .B(B[3]), .C(subtrator_1bit_2_vai_1));
  Subtrator_1Bit subtrator_1bit_2 (
    .S(Saida[2]), .Vai_1(subtrator_1bit_2_vai_1), .A(A[2]), .B(B[2]), .C(subtrator_1bit_3_vai_1));
  // Probe on Saida
  Subtrator_1Bit subtrator_1bit_3 (
    .S(Saida[1]), .Vai_1(subtrator_1bit_3_vai_1), .A(A[1]), .B(B[1]), .C(subtrator_1bit_4_vai_1));
  Subtrator_1Bit subtrator_1bit_4 (.S(Saida[0]), .Vai_1(subtrator_1bit_4_vai_1), .A(A[0]), .B(B[0]), .C(1'b0));
  // Probe on A
endmodule

module \Rotação_Esq  (
  input  [3:0] ABCD,
  input  [1:0] XY,
  output [3:0] ABCD_2
);

  wire and_1_out, and_2_out, and_3_out, and_4_out, and_5_out, and_6_out, and_7_out, and_8_out, and_9_out;

  and and_1 (and_1_out, ~XY[1], ~XY[0], ABCD[3]);  // AND_Gate
  and and_2 (and_2_out, ~XY[1], XY[0], ABCD[2]);  // AND_Gate
  and and_3 (and_3_out, XY[1], ~XY[0], ABCD[1]);  // AND_Gate
  and and_4 (and_4_out, XY[1], XY[0], ABCD[0]);
  and and_5 (and_5_out, ~XY[1], ~XY[0], ABCD[2]);  // AND_Gate
  and and_6 (and_6_out, ~XY[1], XY[0], ABCD[1]);  // AND_Gate
  and and_7 (and_7_out, XY[1], ~XY[0], ABCD[0]);  // AND_Gate
  and and_8 (and_8_out, ~XY[1], ~XY[0], ABCD[1]);  // AND_Gate
  and and_9 (and_9_out, ~XY[1], XY[0], ABCD[0]);  // AND_Gate
  and and_10 (ABCD_2[0], ~XY[1], ~XY[0], ABCD[0]);  // AND_Gate
  or or_1 (ABCD_2[3], and_1_out, and_2_out, and_3_out, and_4_out);
  or or_2 (ABCD_2[2], and_5_out, and_6_out, and_7_out);
  or or_3 (ABCD_2[1], and_8_out, and_9_out);
endmodule

module \Rotação_Dir  (
  input  [3:0] ABCD,
  input  [1:0] XY,
  output [3:0] ABCD_2
);

  wire and_1_out, and_2_out, and_3_out, and_4_out, and_5_out, and_6_out, and_7_out, and_8_out, and_9_out;

  and and_1 (and_1_out, ~XY[1], ~XY[0], ABCD[0]);  // AND_Gate
  and and_2 (and_2_out, ~XY[1], XY[0], ABCD[1]);  // AND_Gate
  and and_3 (and_3_out, XY[1], ~XY[0], ABCD[2]);  // AND_Gate
  and and_4 (and_4_out, XY[1], XY[0], ABCD[3]);
  and and_5 (and_5_out, ~XY[1], ~XY[0], ABCD[1]);  // AND_Gate
  and and_6 (and_6_out, ~XY[1], XY[0], ABCD[2]);  // AND_Gate
  and and_7 (and_7_out, XY[1], ~XY[0], ABCD[3]);  // AND_Gate
  and and_8 (and_8_out, ~XY[1], ~XY[0], ABCD[2]);  // AND_Gate
  and and_9 (and_9_out, ~XY[1], XY[0], ABCD[3]);  // AND_Gate
  and and_10 (ABCD_2[3], ~XY[1], ~XY[0], ABCD[3]);  // AND_Gate
  or or_1 (ABCD_2[0], and_1_out, and_2_out, and_3_out, and_4_out);
  or or_2 (ABCD_2[1], and_5_out, and_6_out, and_7_out);
  or or_3 (ABCD_2[2], and_8_out, and_9_out);
endmodule
